# Fritzing sketch PiPT1000 (saved by Fritzing 0.9.6b)

parts:
  MCU1 = Raspberry Pi Zero
  Bauteil1 = OLED Monochrome 128x64 0.96 inch [part_number=326]
  Bauteil2 = Adafruit MAX31865 RTD Sensor Breakout [part_number="Adafruit #3328"]
  Bauteil3 = Adafruit MAX31865 RTD Sensor Breakout [part_number="Adafruit #3328"]
  C1 = Ceramic Capacitor [capacitance=100nF voltage=35V package="100 mil [THT, multilayer]"]
  C2 = Ceramic Capacitor [capacitance=100nF voltage=35V package="100 mil [THT, multilayer]"]
  M1 = RioRand LM2596
  JACK1 = 2.1mm Barrel Jack with Terminal Block
  U1 = SWITCH_SPDT [package=kps-1290]
  LED1 = LED - 5mm [color="Red (633nm)" current=0.030 package="5 mm [THT]"]
  LED2 = LED - 5mm [color="Green (555nm)" current=0.030 package="5 mm [THT]"]
  R1 = Resistor [tolerance=±5% power=0.25 resistance=220 package=THT]
  R2 = Resistor [tolerance=±5% power=0.25 resistance=220 package=THT]

nets:
  VIN: MCU1.pin_1, MCU1.pin_17, Bauteil1.VIN, Bauteil2.VIN, Bauteil3.VIN
  N1: MCU1.pin_2, M1.Pin_3
  N2: MCU1.pin_3, Bauteil1.MOSI_SDA
  N3: MCU1.pin_5, Bauteil1.SCLK_SCK
  GND: MCU1.pin_6, MCU1.pin_9, MCU1.pin_20, MCU1.pin_25, Bauteil1.GND, Bauteil2.GND, Bauteil3.GND, M1.Pin_4, U1.P, R1.Pin_0, R2.Pin_1
  N4: MCU1.pin_7, LED2.anode
  N5: MCU1.pin_12, LED1.anode
  N6: MCU1.pin_15, Bauteil2.CS
  N7: MCU1.pin_18, U1.O
  N8: MCU1.pin_19, Bauteil2.SDI, Bauteil3.SDI
  N9: MCU1.pin_21, Bauteil2.SDO, Bauteil3.SDO
  N10: MCU1.pin_22, U1.S
  N11: MCU1.pin_23, Bauteil2.SCLK, Bauteil3.SCLK
  N12: MCU1.pin_26, Bauteil3.CS
  N13: Bauteil2.RTDIN+, Bauteil2.FORCE+, C2.1
  N14: Bauteil2.FORCE-, Bauteil2.RTDIN-, C2.0
  N15: Bauteil3.RTDIN+, Bauteil3.FORCE+, C1.1
  N16: Bauteil3.FORCE-, Bauteil3.RTDIN-, C1.0
  N17: M1.Pin_1, JACK1.NEG
  N18: M1.Pin_2, JACK1.POS
  N19: LED1.cathode, R1.Pin_1
  N20: LED2.cathode, R2.Pin_0

custom parts:
  OLED Monochrome 128x64 0.96 inch: These displays are small, only about 1" diameter, but very readable due to the high contrast of an OLED display. This display is made of 128x64 individual white OLED pixels, each one is turned on or off by the controller chip. Because the display makes its own light, no backlight is required. This reduces the power required to run the OLED and is why the display has such high contrast; we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
  Adafruit MAX31865 RTD Sensor Breakout: For precision temperature sensing, nothing beats a Platinum RTD. Resistance temperature detectors (RTDs) are temperature sensors that contain a resistor that changes resistance value as its temperature changes, basically a kind of thermistor. In this sensor, the resistor is actually a small strip of Platinum with a resistance of 100 ohms at 0°C, thus the name PT100. Compared to most NTC/PTC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
